# Fritzing sketch Laser Susan Schematic (saved by Fritzing 0.9.2b)
breadboards: 1

parts:
  Part1 = Arduino Uno (Rev3)
  M1 = DC Motor
  Q1 = NPN-Transistor [package="TO92 [THT]"]
  R1 = Resistor [tolerance=±5% resistance=220 package=THT]
  Power_plug1 = Power plug
  R2 = Resistor [tolerance=±5% resistance=220 package=THT]
  J1 = Infrared Proximity Sensor
  R3 = Resistor [tolerance=±5% resistance=220 package=THT]
  R4 = Resistor [tolerance=±5% resistance=220 package=THT]
  LED1 = LED - 5mm [color="Red (633nm)" package="5 mm [THT]"]

nets:
  N1: Part1.A0, R2.Pin_1
  N2: Part1.D11_PWM/MOSI, R4.Pin_0
  N3: Part1.D13/SCK, R1.Pin_0
  GND: Part1.GND, Q1.E, J1.GND, R3.Pin_1, LED1.cathode
  N4: Part1.D2, J1.Vout, R3.Pin_0
  5V: Part1.5V, J1.Vcc
  N5: M1.pin_1, Power_plug1.VCC
  N6: M1.pin_2, Q1.C
  N7: Q1.B, R1.Pin_1
  N8: R4.Pin_1, LED1.anode

notes:
  < crude, represents output to laser
  proximity sensor that detects a well
  input from LCD keypad shield button
  < this is crude, but represents the switch that controls the turntable motor
  pull-down resistor
